# Fritzing sketch Schematic (saved by Fritzing 0.8.3b)
circuit board: 16.9333cm x 5.64444cm
breadboards: 1

parts:
  16_x_2_generic_LCD = LCD screen
  U1 = atmega328 [package=dip]
  SD_card_breakout = mystery part, 6 pins [chip_label=?]

nets:
  VSS: 16_x_2_generic_LCD.VSS, 16_x_2_generic_LCD.R/W, 16_x_2_generic_LCD.LED-, U1.GND, SD_card_breakout.pin1
  VDD: 16_x_2_generic_LCD.VDD, U1.VCC
  N1: 16_x_2_generic_LCD.V0, U1.D6_(PWM)
  N2: 16_x_2_generic_LCD.RS, U1.D9_(PWM)
  N3: 16_x_2_generic_LCD.E, U1.D7
  N4: 16_x_2_generic_LCD.DB4, U1.D5_(PWM)
  N5: 16_x_2_generic_LCD.DB5, U1.D4
  N6: 16_x_2_generic_LCD.DB6, U1.D3_(PWM)
  N7: 16_x_2_generic_LCD.DB7, U1.D2
  N8: 16_x_2_generic_LCD.LED+, U1.D10_(PWM)
  N9: U1.D8, SD_card_breakout.pin3
  N10: U1.D11_(PWM), SD_card_breakout.pin4
  N11: U1.D12, SD_card_breakout.pin6
  N12: U1.D13, SD_card_breakout.pin5
